# Fritzing sketch register (saved by Fritzing 0.9.4)
breadboards: 1

parts:
  IC1 = IC, DIP package, 20 pins [chip_label=____________245]
  IC2 = IC, DIP package, 20 pins [chip_label=377]
  R7 = Resistor [tolerance=±5% resistance=150 package=THT]
  R8 = Resistor [tolerance=±5% resistance=150 package=THT]
  R9 = Resistor [tolerance=±5% resistance=150 package=THT]
  R10 = Resistor [tolerance=±5% resistance=150 package=THT]
  R11 = Resistor [tolerance=±5% resistance=150 package=THT]
  R12 = Resistor [tolerance=±5% resistance=150 package=THT]
  R13 = Resistor [tolerance=±5% resistance=150 package=THT]
  R14 = Resistor [tolerance=±5% resistance=150 package=THT]
  IC3 = IC, DIP package, 20 pins [chip_label=___________377]
  IC4 = IC, DIP package, 20 pins [chip_label=245]
  R15 = Resistor [tolerance=±5% resistance=150 package=THT]
  R16 = Resistor [tolerance=±5% resistance=150 package=THT]
  R17 = Resistor [tolerance=±5% resistance=150 package=THT]
  R18 = Resistor [tolerance=±5% resistance=150 package=THT]
  R19 = Resistor [tolerance=±5% resistance=150 package=THT]
  R20 = Resistor [tolerance=±5% resistance=150 package=THT]
  R21 = Resistor [tolerance=±5% resistance=150 package=THT]
  R22 = Resistor [tolerance=±5% resistance=150 package=THT]
  R23 = Resistor [tolerance=±5% resistance=150 package=THT]
  R24 = Resistor [tolerance=±5% resistance=150 package=THT]

nets:
  N1: IC1.pin1, IC1.pin10, IC2.pin10, R7.Pin_1, R8.Pin_1, R9.Pin_1, R10.Pin_1, IC3.pin10, IC4.pin1, IC4.pin10, R15.Pin_1, R16.Pin_1, R17.Pin_1, R18.Pin_1
  N2: IC1.pin2, IC1.pin9, IC2.pin3, IC2.pin13
  N3: IC1.pin3, IC2.pin18
  N4: IC1.pin4, IC2.pin4
  N5: IC1.pin5, IC2.pin17
  N6: IC1.pin6, IC2.pin7
  N7: IC1.pin7, IC2.pin14
  N8: IC1.pin8, IC2.pin8
  N9: IC1.pin11, IC2.pin12
  N10: IC1.pin12, IC2.pin9
  N11: IC1.pin13, IC2.pin15
  N12: IC1.pin14, IC2.pin6
  N13: IC1.pin15, IC2.pin16
  N14: IC1.pin16, IC2.pin5
  N15: IC1.pin17, IC2.pin19
  N16: IC1.pin18, IC2.pin2
  N17: IC1.pin19, IC1.pin20, IC2.pin20, IC3.pin20, IC4.pin20, R23.Pin_0
  N18: IC2.pin1, IC3.pin1, R23.Pin_1
  N19: IC2.pin11, IC4.pin19, R24.Pin_0
  N20: R11.Pin_0, R12.Pin_0, R13.Pin_0, R14.Pin_0, R19.Pin_0, R20.Pin_0, R21.Pin_0, R22.Pin_0
  N21: IC3.pin2, IC4.pin17
  N22: IC3.pin3, IC4.pin3
  N23: IC3.pin4, IC4.pin5
  N24: IC3.pin5, IC4.pin15
  N25: IC3.pin6, IC4.pin13
  N26: IC3.pin7, IC4.pin7
  N27: IC3.pin8, IC3.pin18, IC4.pin2, IC4.pin9
  N28: IC3.pin9, IC4.pin11
  N29: IC3.pin12, IC4.pin12
  N30: IC3.pin13, IC4.pin8
  N31: IC3.pin14, IC4.pin6
  N32: IC3.pin15, IC4.pin14
  N33: IC3.pin16, IC4.pin16
  N34: IC3.pin17, IC4.pin4
  N35: IC3.pin19, IC4.pin18

notes:
  W
  OE
  CLK
