# Fritzing sketch register2 (saved by Fritzing 0.9.4)
breadboards: 2

parts:
  IC1 = IC, DIP package, 20 pins [chip_label=____________245]
  IC2 = IC, DIP package, 20 pins [chip_label=377]
  R7 = Resistor [tolerance=±5% resistance=150 package=THT]
  R8 = Resistor [tolerance=±5% resistance=150 package=THT]
  R9 = Resistor [tolerance=±5% resistance=150 package=THT]
  R10 = Resistor [tolerance=±5% resistance=150 package=THT]
  R11 = Resistor [tolerance=±5% resistance=150 package=THT]
  R12 = Resistor [tolerance=±5% resistance=150 package=THT]
  R13 = Resistor [tolerance=±5% resistance=150 package=THT]
  R14 = Resistor [tolerance=±5% resistance=150 package=THT]
  IC3 = IC, DIP package, 20 pins [chip_label=___________377]
  IC4 = IC, DIP package, 20 pins [chip_label=245]
  R15 = Resistor [tolerance=±5% resistance=150 package=THT]
  R16 = Resistor [tolerance=±5% resistance=150 package=THT]
  R17 = Resistor [tolerance=±5% resistance=150 package=THT]
  R18 = Resistor [tolerance=±5% resistance=150 package=THT]
  R19 = Resistor [tolerance=±5% resistance=150 package=THT]
  R20 = Resistor [tolerance=±5% resistance=150 package=THT]
  R21 = Resistor [tolerance=±5% resistance=150 package=THT]
  R22 = Resistor [tolerance=±5% resistance=150 package=THT]
  R23 = Resistor [tolerance=±5% resistance=150 package=THT]
  R24 = Resistor [tolerance=±5% resistance=150 package=THT]
  IC6 = IC, DIP package, 20 pins [chip_label=377]
  IC7 = IC, DIP package, 20 pins [chip_label=245]
  IC8 = IC, DIP package, 20 pins [chip_label=245]
  IC5 = IC, DIP package, 20 pins [chip_label=377]

nets:
  N1: IC1.pin1, IC1.pin10, IC2.pin10, R7.Pin_1, R8.Pin_1, R9.Pin_1, R10.Pin_1, IC3.pin10, IC4.pin1, IC4.pin10, R15.Pin_1, R16.Pin_1, R17.Pin_1, R18.Pin_1
  N2: IC1.pin2, IC1.pin9, IC2.pin3, IC2.pin13
  N3: IC1.pin3, IC2.pin18
  N4: IC1.pin4, IC2.pin4
  N5: IC1.pin5, IC2.pin17
  N6: IC1.pin6, IC2.pin7
  N7: IC1.pin7, IC2.pin14
  N8: IC1.pin8, IC2.pin8
  N9: IC1.pin11, IC2.pin12
  N10: IC1.pin12, IC2.pin9
  N11: IC1.pin13, IC2.pin15
  N12: IC1.pin14, IC2.pin6
  N13: IC1.pin15, IC2.pin16
  N14: IC1.pin16, IC2.pin5
  N15: IC1.pin17, IC2.pin19
  N16: IC1.pin18, IC2.pin2
  N17: IC1.pin19, IC1.pin20, IC2.pin20, IC3.pin20, IC4.pin19, IC4.pin20, R23.Pin_0, R24.Pin_0
  N18: IC2.pin1, IC3.pin1, R23.Pin_1
  N19: R11.Pin_0, R12.Pin_0, R13.Pin_0, R14.Pin_0, R19.Pin_0, R20.Pin_0, R21.Pin_0, R22.Pin_0
  N20: IC3.pin2, IC4.pin17
  N21: IC3.pin3, IC4.pin3
  N22: IC3.pin4, IC4.pin5
  N23: IC3.pin5, IC4.pin15
  N24: IC3.pin6, IC4.pin13
  N25: IC3.pin7, IC4.pin7
  N26: IC3.pin8, IC3.pin18, IC4.pin2, IC4.pin9
  N27: IC3.pin9, IC4.pin11
  N28: IC3.pin12, IC4.pin12
  N29: IC3.pin13, IC4.pin8
  N30: IC3.pin14, IC4.pin6
  N31: IC3.pin15, IC4.pin14
  N32: IC3.pin16, IC4.pin16
  N33: IC3.pin17, IC4.pin4
  N34: IC3.pin19, IC4.pin18
  N35: IC6.pin1, IC5.pin1
  N36: IC6.pin2, IC7.pin18
  N37: IC6.pin3, IC6.pin4
  N38: IC6.pin5, IC7.pin16
  N39: IC6.pin6, IC7.pin14
  N40: IC6.pin7, IC6.pin8
  N41: IC6.pin9, IC7.pin12
  N42: IC6.pin10, IC7.pin1, IC7.pin10, IC8.pin1, IC8.pin10, IC5.pin10
  N43: IC6.pin11, IC5.pin11
  N44: IC6.pin12, IC7.pin11
  N45: IC6.pin13, IC6.pin14
  N46: IC6.pin15, IC7.pin13
  N47: IC6.pin16, IC7.pin15
  N48: IC6.pin17, IC6.pin18
  N49: IC6.pin19, IC7.pin17
  N50: IC6.pin20, IC7.pin20, IC8.pin20, IC5.pin20
  N51: IC7.pin2, IC7.pin9
  N52: IC7.pin19, IC8.pin19
  N53: IC8.pin2, IC8.pin9
  N54: IC8.pin11, IC5.pin15
  N55: IC8.pin12, IC5.pin6
  N56: IC8.pin13, IC5.pin12
  N57: IC8.pin14, IC5.pin9
  N58: IC8.pin15, IC5.pin19
  N59: IC8.pin16, IC5.pin2
  N60: IC8.pin17, IC5.pin16
  N61: IC8.pin18, IC5.pin5
  N62: IC5.pin3, IC5.pin4
  N63: IC5.pin7, IC5.pin8
  N64: IC5.pin13, IC5.pin14
  N65: IC5.pin17, IC5.pin18

notes:
  W
  OE
  CLK
