# Fritzing sketch register_control (saved by Fritzing 0.9.4)
breadboards: 7

parts:
  IC9 = IC, DIP package, 20 pins [chip_label=377]
  IC10 = IC, DIP package, 20 pins [chip_label=377]
  IC11 = IC, DIP package, 20 pins [chip_label=245]
  IC12 = IC, DIP package, 20 pins [chip_label=245]
  IC13 = IC, DIP package, 20 pins [chip_label=BUF]
  IC17 = IC, DIP package, 16 pins [chip_label=MUX]
  IC18 = IC, DIP package, 16 pins [chip_label=MUX]
  IC19 = IC, DIP package, 16 pins [chip_label=MUX]
  IC20 = IC, DIP package, 16 pins [chip_label=ADD]
  IC21 = IC, DIP package, 16 pins [chip_label=ADD]
  IC22 = IC, DIP package, 20 pins [chip_label="BUF sum out"]
  IC25 = IC, DIP package, 16 pins [chip_label=DEMUX]
  IC26 = IC, DIP package, 16 pins [chip_label=DEMUX]
  IC27 = IC, DIP package, 20 pins
  IC28 = IC, DIP package, 20 pins [chip_label="BUF sum out"]
  IC29 = IC, DIP package, 20 pins [chip_label=BUF]
  IC30 = IC, DIP package, 14 pins [chip_label=XOR]
  IC32 = IC, DIP package, 16 pins [chip_label=MUX]
  IC23 = IC, DIP package, 20 pins
  IC40 = IC, DIP package, 20 pins [chip_label="BUF IR -> bus"]
  IC41 = IC, DIP package, 20 pins [chip_label=FF]
  IC42 = IC, DIP package, 16 pins [chip_label=ADD]
  IC43 = IC, DIP package, 16 pins [chip_label=ADD]
  IC44 = IC, DIP package, 20 pins [chip_label="BUF IR -> bus"]
  IC45 = IC, DIP package, 20 pins [chip_label=FF]

nets:
  N1: IC9.pin1, IC10.pin1, IC25.pin7
  N2: IC9.pin2, IC11.pin16
  N3: IC9.pin3, IC9.pin4, IC22.pin2, IC22.pin4, IC23.pin16, IC23.pin18
  N4: IC9.pin5, IC11.pin18
  N5: IC9.pin6, IC11.pin12
  N6: IC9.pin7, IC9.pin8, IC22.pin6, IC22.pin8, IC23.pin12, IC23.pin14
  N7: IC9.pin9, IC11.pin14
  N8: IC9.pin10, IC10.pin10, IC11.pin1, IC11.pin10, IC12.pin1, IC12.pin10, IC13.pin11, IC13.pin12, IC13.pin13, IC13.pin14, IC13.pin15, IC13.pin16, IC13.pin17, IC13.pin18, IC25.pin5, IC25.pin8, IC29.pin11, IC29.pin12, IC29.pin13, IC29.pin14, IC29.pin15, IC29.pin16, IC29.pin17, IC29.pin18
  N9: IC9.pin11, IC10.pin11
  N10: IC9.pin12, IC11.pin13
  N11: IC9.pin13, IC9.pin14, IC22.pin7, IC22.pin9, IC23.pin11, IC23.pin13
  N12: IC9.pin15, IC11.pin11
  N13: IC9.pin16, IC11.pin17
  N14: IC9.pin17, IC9.pin18, IC22.pin3, IC22.pin5, IC23.pin15, IC23.pin17
  N15: IC9.pin19, IC11.pin15
  N16: IC9.pin20, IC10.pin20, IC11.pin20, IC12.pin20
  N17: IC10.pin2, IC12.pin15
  N18: IC10.pin3, IC27.pin17, IC28.pin3
  N19: IC10.pin4, IC27.pin15, IC28.pin5
  N20: IC10.pin5, IC12.pin17
  N21: IC10.pin6, IC12.pin11
  N22: IC10.pin7, IC27.pin13, IC28.pin7
  N23: IC10.pin8, IC27.pin11, IC28.pin9
  N24: IC10.pin9, IC12.pin13
  N25: IC10.pin12, IC12.pin14
  N26: IC10.pin13, IC10.pin14, IC27.pin12, IC27.pin14, IC28.pin6, IC28.pin8
  N27: IC10.pin15, IC12.pin12
  N28: IC10.pin16, IC12.pin18
  N29: IC10.pin17, IC10.pin18, IC27.pin16, IC27.pin18, IC28.pin2, IC28.pin4
  N30: IC10.pin19, IC12.pin16
  N31: IC11.pin2, IC11.pin9, IC13.pin2, IC13.pin9, IC20.pin6, IC21.pin12
  N32: IC11.pin19, IC12.pin19, IC26.pin7
  N33: IC12.pin2, IC12.pin9, IC29.pin2, IC29.pin9, IC42.pin12, IC43.pin6
  N34: IC13.pin1, IC13.pin10, IC20.pin7, IC20.pin8, IC26.pin5, IC26.pin8, IC29.pin1, IC29.pin10, IC43.pin8
  N35: IC13.pin3, IC21.pin15
  N36: IC13.pin4, IC21.pin3
  N37: IC13.pin5, IC21.pin6
  N38: IC13.pin6, IC20.pin11
  N39: IC13.pin7, IC20.pin15
  N40: IC13.pin8, IC20.pin3
  N41: IC13.pin19, IC26.pin15, IC29.pin19
  N42: IC13.pin20, IC25.pin6, IC26.pin16, IC29.pin20
  N43: IC17.pin1, IC18.pin1, IC19.pin1, IC32.pin1
  N44: IC17.pin2, IC17.pin5, IC17.pin8, IC18.pin3, IC18.pin6, IC18.pin8, IC19.pin3, IC19.pin6, IC19.pin8, IC27.pin10, IC32.pin2, IC32.pin5, IC32.pin8, IC23.pin10
  N45: IC17.pin3, IC40.pin18, IC41.pin16
  N46: IC17.pin4, IC21.pin2
  N47: IC17.pin6, IC40.pin17, IC41.pin2
  N48: IC17.pin7, IC21.pin5
  N49: IC17.pin9, IC21.pin11
  N50: IC17.pin10, IC40.pin15, IC41.pin19
  N51: IC17.pin11, IC17.pin13, IC19.pin7, IC19.pin10, IC19.pin13, IC21.pin8, IC22.pin1, IC28.pin1, IC28.pin10, IC30.pin7, IC32.pin11, IC32.pin14, IC42.pin8, IC43.pin14
  N52: IC17.pin12, IC21.pin14
  N53: IC17.pin14, IC40.pin16, IC41.pin5
  N54: IC17.pin15, IC18.pin15, IC19.pin15, IC32.pin15
  N55: IC17.pin16, IC18.pin10, IC18.pin13, IC18.pin16, IC19.pin16, IC20.pin16, IC27.pin20, IC32.pin16, IC23.pin20, IC43.pin16
  N56: IC18.pin2, IC40.pin12, IC41.pin15
  N57: IC18.pin4, IC20.pin12
  N58: IC18.pin5, IC40.pin11, IC41.pin9
  N59: IC18.pin7, IC20.pin14
  N60: IC18.pin9, IC20.pin2
  N61: IC18.pin11, IC40.pin13, IC41.pin12
  N62: IC18.pin12, IC20.pin5
  N63: IC18.pin14, IC40.pin14, IC41.pin6
  N64: IC19.pin2, IC44.pin12, IC45.pin9
  N65: IC19.pin4, IC43.pin11
  N66: IC19.pin5, IC44.pin11, IC45.pin12
  N67: IC19.pin9, IC43.pin2
  N68: IC19.pin11, IC44.pin13, IC45.pin6
  N69: IC19.pin12, IC43.pin5
  N70: IC19.pin14, IC44.pin14, IC45.pin15
  N71: IC20.pin1, IC22.pin14
  N72: IC20.pin4, IC22.pin13
  N73: IC20.pin9, IC21.pin7
  N74: IC20.pin10, IC22.pin12
  N75: IC20.pin13, IC22.pin11
  N76: IC21.pin1, IC22.pin18
  N77: IC21.pin4, IC22.pin17
  N78: IC21.pin9, IC43.pin7
  N79: IC21.pin10, IC22.pin16
  N80: IC21.pin13, IC22.pin15
  N81: IC21.pin16, IC22.pin19, IC25.pin16, IC26.pin6, IC27.pin1, IC28.pin19, IC28.pin20, IC30.pin9, IC30.pin10, IC30.pin14, IC23.pin1, IC42.pin16
  N82: IC27.pin19, IC30.pin8, IC23.pin19
  N83: IC28.pin11, IC43.pin13
  N84: IC28.pin12, IC43.pin10
  N85: IC28.pin13, IC43.pin4
  N86: IC28.pin14, IC43.pin1
  N87: IC28.pin15, IC42.pin13
  N88: IC28.pin16, IC42.pin10
  N89: IC28.pin17, IC42.pin4
  N90: IC28.pin18, IC42.pin1
  N91: IC29.pin3, IC42.pin15
  N92: IC29.pin4, IC42.pin3
  N93: IC29.pin5, IC42.pin6
  N94: IC29.pin6, IC43.pin12
  N95: IC29.pin7, IC43.pin15
  N96: IC29.pin8, IC43.pin3
  N97: IC32.pin3, IC44.pin18, IC45.pin2
  N98: IC32.pin4, IC42.pin2
  N99: IC32.pin6, IC44.pin17, IC45.pin19
  N100: IC32.pin7, IC42.pin5
  N101: IC32.pin9, IC42.pin11
  N102: IC32.pin10, IC44.pin15, IC45.pin5
  N103: IC32.pin12, IC42.pin14
  N104: IC32.pin13, IC44.pin16, IC45.pin16
  N105: IC40.pin1, IC40.pin10, IC41.pin10, IC44.pin1, IC44.pin10, IC45.pin10
  N106: IC40.pin2, IC41.pin18
  N107: IC40.pin3, IC41.pin3
  N108: IC40.pin4, IC41.pin4
  N109: IC40.pin5, IC41.pin17
  N110: IC40.pin6, IC41.pin8
  N111: IC40.pin7, IC41.pin14
  N112: IC40.pin8, IC41.pin13
  N113: IC40.pin9, IC41.pin7
  N114: IC40.pin20, IC41.pin20, IC44.pin20, IC45.pin20
  N115: IC42.pin7, IC43.pin9
  N116: IC44.pin2, IC45.pin3
  N117: IC44.pin3, IC45.pin18
  N118: IC44.pin4, IC45.pin17
  N119: IC44.pin5, IC45.pin4
  N120: IC44.pin6, IC45.pin14
  N121: IC44.pin7, IC45.pin7
  N122: IC44.pin8, IC45.pin8
  N123: IC44.pin9, IC45.pin13

notes:
  W
  OE
  CLK
  TODO: swap A/B on ADD
  TODO: constant, carry
