# Fritzing sketch register_control_layered (saved by Fritzing 0.9.4)
breadboards: 6

parts:
  IC9 = IC, DIP package, 20 pins [chip_label=377]
  IC10 = IC, DIP package, 20 pins [chip_label=377]
  IC11 = IC, DIP package, 20 pins [chip_label=245]
  IC12 = IC, DIP package, 20 pins [chip_label=245]
  IC13 = IC, DIP package, 20 pins [chip_label=BUF]
  IC17 = IC, DIP package, 16 pins [chip_label=MUX]
  IC18 = IC, DIP package, 16 pins [chip_label=MUX]
  IC19 = IC, DIP package, 16 pins [chip_label=MUX]
  IC20 = IC, DIP package, 16 pins [chip_label=ADD]
  IC21 = IC, DIP package, 16 pins [chip_label=ADD]
  IC22 = IC, DIP package, 20 pins [chip_label="BUF sum out"]
  IC25 = IC, DIP package, 16 pins [chip_label=DEMUX]
  IC26 = IC, DIP package, 16 pins [chip_label=DEMUX]
  IC27 = IC, DIP package, 20 pins
  IC28 = IC, DIP package, 20 pins [chip_label="BUF sum out"]
  IC29 = IC, DIP package, 20 pins [chip_label=BUF]
  IC30 = IC, DIP package, 14 pins [chip_label=XOR]
  IC32 = IC, DIP package, 16 pins [chip_label=MUX]
  IC23 = IC, DIP package, 20 pins
  IC42 = IC, DIP package, 16 pins [chip_label=ADD]
  IC43 = IC, DIP package, 16 pins [chip_label=ADD]
  IC44 = IC, DIP package, 20 pins [chip_label=377]
  IC46 = IC, DIP package, 20 pins [chip_label=245]
  IC47 = IC, DIP package, 20 pins [chip_label=377]
  IC48 = IC, DIP package, 20 pins [chip_label=245]

nets:
  N1: IC9.pin1, IC10.pin1, IC25.pin7
  N2: IC9.pin2, IC11.pin16
  N3: IC9.pin3, IC9.pin4, IC22.pin2, IC22.pin4, IC23.pin16, IC23.pin18
  N4: IC9.pin5, IC11.pin18
  N5: IC9.pin6, IC11.pin12
  N6: IC9.pin7, IC9.pin8, IC22.pin6, IC22.pin8, IC23.pin12, IC23.pin14
  N7: IC9.pin9, IC11.pin14
  N8: IC9.pin10, IC10.pin10, IC11.pin1, IC11.pin10, IC12.pin1, IC12.pin10, IC13.pin11, IC13.pin12, IC13.pin13, IC13.pin14, IC13.pin15, IC13.pin16, IC13.pin17, IC13.pin18, IC25.pin5, IC25.pin8, IC29.pin11, IC29.pin12, IC29.pin13, IC29.pin14, IC29.pin15, IC29.pin16, IC29.pin17, IC29.pin18
  N9: IC9.pin11, IC10.pin11
  N10: IC9.pin12, IC11.pin13
  N11: IC9.pin13, IC9.pin14, IC22.pin7, IC22.pin9, IC23.pin11, IC23.pin13
  N12: IC9.pin15, IC11.pin11
  N13: IC9.pin16, IC11.pin17
  N14: IC9.pin17, IC9.pin18, IC22.pin3, IC22.pin5, IC23.pin15, IC23.pin17
  N15: IC9.pin19, IC11.pin15
  N16: IC9.pin20, IC10.pin7, IC10.pin8, IC10.pin20, IC11.pin20, IC12.pin20, IC27.pin11, IC27.pin13, IC28.pin7, IC28.pin9
  N17: IC10.pin2, IC12.pin15
  N18: IC10.pin3, IC27.pin17, IC28.pin3
  N19: IC10.pin4, IC10.pin17, IC27.pin15, IC27.pin16, IC28.pin4, IC28.pin5
  N20: IC10.pin5, IC12.pin17
  N21: IC10.pin6, IC12.pin11
  N22: IC10.pin9, IC12.pin13
  N23: IC10.pin12, IC12.pin14
  N24: IC10.pin13, IC10.pin14, IC27.pin12, IC27.pin14, IC28.pin6, IC28.pin8
  N25: IC10.pin15, IC12.pin12
  N26: IC10.pin16, IC12.pin18
  N27: IC10.pin18, IC27.pin18, IC28.pin2
  N28: IC10.pin19, IC12.pin16
  N29: IC11.pin2, IC11.pin9, IC13.pin2, IC13.pin9, IC20.pin6, IC21.pin12
  N30: IC11.pin3, IC13.pin3, IC21.pin15
  N31: IC11.pin4, IC13.pin4, IC21.pin3
  N32: IC11.pin5, IC13.pin5, IC21.pin6
  N33: IC11.pin6, IC13.pin6, IC20.pin11
  N34: IC11.pin7, IC13.pin7, IC20.pin15
  N35: IC11.pin8, IC13.pin8, IC20.pin3
  N36: IC11.pin19, IC12.pin19, IC26.pin7
  N37: IC12.pin2, IC12.pin9, IC29.pin2, IC29.pin9, IC42.pin12, IC43.pin6
  N38: IC12.pin3, IC29.pin3, IC42.pin15
  N39: IC12.pin4, IC29.pin4, IC42.pin2
  N40: IC12.pin5, IC29.pin5, IC42.pin6
  N41: IC12.pin6, IC29.pin6, IC43.pin12
  N42: IC12.pin7, IC29.pin7, IC43.pin15
  N43: IC12.pin8, IC29.pin8, IC43.pin3
  N44: IC13.pin1, IC13.pin10, IC20.pin7, IC20.pin8, IC26.pin5, IC26.pin8, IC29.pin1, IC29.pin10, IC42.pin11, IC42.pin14, IC43.pin8
  N45: IC13.pin19, IC26.pin15, IC29.pin19
  N46: IC13.pin20, IC25.pin6, IC26.pin16, IC29.pin20
  N47: IC17.pin1, IC18.pin1, IC19.pin1, IC27.pin19, IC30.pin8, IC32.pin1, IC23.pin19, IC44.pin20, IC46.pin20, IC47.pin20, IC48.pin20
  N48: IC17.pin2, IC47.pin12, IC48.pin13
  N49: IC17.pin3, IC17.pin5, IC17.pin8, IC18.pin2, IC18.pin5, IC18.pin8, IC19.pin2, IC19.pin6, IC19.pin8, IC27.pin10, IC32.pin5, IC32.pin8, IC23.pin10
  N50: IC17.pin4, IC21.pin2
  N51: IC17.pin6, IC44.pin5, IC46.pin18
  N52: IC17.pin7, IC21.pin5
  N53: IC17.pin9, IC21.pin11
  N54: IC17.pin10, IC47.pin15, IC48.pin11
  N55: IC17.pin11, IC17.pin13, IC19.pin7, IC19.pin10, IC19.pin13, IC21.pin8, IC22.pin1, IC28.pin1, IC28.pin10, IC30.pin7, IC42.pin3, IC42.pin8, IC43.pin14
  N56: IC17.pin12, IC21.pin14
  N57: IC17.pin14, IC47.pin6, IC48.pin12
  N58: IC17.pin15, IC18.pin15, IC19.pin15, IC32.pin15
  N59: IC17.pin16, IC18.pin10, IC18.pin13, IC18.pin16, IC19.pin16, IC20.pin16, IC27.pin20, IC32.pin16, IC23.pin20, IC43.pin16
  N60: IC18.pin3, IC44.pin16, IC46.pin17
  N61: IC18.pin4, IC20.pin12
  N62: IC18.pin6, IC44.pin9, IC46.pin14
  N63: IC18.pin7, IC20.pin14
  N64: IC18.pin9, IC20.pin2
  N65: IC18.pin11, IC44.pin19, IC46.pin15
  N66: IC18.pin12, IC20.pin5
  N67: IC18.pin14, IC44.pin2, IC46.pin16
  N68: IC19.pin3, IC47.pin16, IC48.pin17
  N69: IC19.pin4, IC43.pin11
  N70: IC19.pin5, IC47.pin2, IC48.pin16
  N71: IC19.pin9, IC43.pin2
  N72: IC19.pin11, IC47.pin19, IC48.pin15
  N73: IC19.pin12, IC43.pin5
  N74: IC19.pin14, IC47.pin9, IC48.pin14
  N75: IC20.pin1, IC22.pin14
  N76: IC20.pin4, IC22.pin13
  N77: IC20.pin9, IC21.pin7
  N78: IC20.pin10, IC22.pin12
  N79: IC20.pin13, IC22.pin11
  N80: IC21.pin1, IC22.pin18
  N81: IC21.pin4, IC22.pin17
  N82: IC21.pin9, IC43.pin7
  N83: IC21.pin10, IC22.pin16
  N84: IC21.pin13, IC22.pin15
  N85: IC21.pin16, IC25.pin16, IC26.pin6, IC28.pin20, IC30.pin14, IC42.pin16
  N86: IC22.pin19, IC27.pin1, IC28.pin19, IC30.pin9, IC23.pin1
  N87: IC27.pin2, IC27.pin9
  N88: IC28.pin11, IC43.pin13
  N89: IC28.pin12, IC43.pin10
  N90: IC28.pin13, IC43.pin4
  N91: IC28.pin14, IC43.pin1
  N92: IC28.pin15, IC42.pin13
  N93: IC28.pin16, IC42.pin10
  N94: IC28.pin17, IC42.pin4
  N95: IC28.pin18, IC42.pin1
  N96: IC32.pin6, IC47.pin5, IC48.pin18
  N97: IC32.pin7, IC42.pin5
  N98: IC42.pin7, IC43.pin9
  N99: IC44.pin1, IC47.pin1
  N100: IC44.pin6, IC46.pin12
  N101: IC44.pin10, IC46.pin1, IC46.pin10, IC47.pin10, IC48.pin1, IC48.pin10
  N102: IC44.pin11, IC47.pin11
  N103: IC44.pin12, IC46.pin13
  N104: IC44.pin15, IC46.pin11
  N105: IC46.pin2, IC46.pin9
  N106: IC46.pin19, IC48.pin19

notes:
  W
  OE
  CLK
